# Fritzing sketch Schetch (saved by Fritzing 0.9.3b)
circuit board: 8.46667cm x 5.64444cm
perfboards: 1

parts:
  Part1 = Arduino Uno (Rev3)
  S1 = Toggle Switch [package=THT]
  Pololu_A1 = Pololu A4988 [package=SO16]
  R1 = Resistor [tolerance=±5% resistance=220 package="0402 [SMD]"]
  X1 = DB15 Connector [package=db15]
  U1 = 2-Channel 5v Relay Shield [package=relay-2ch5v10a]
  J1 = Basic Servo
  M1 = Stepper Motor - Bipolar
  VCC1 = Battery
  C1 = Capacitor Polarized [package=cpol-radial-10uf-25v]
  J2 = Screw terminal - 2 pins [package=THT]
  J3 = Screw terminal - 2 pins [package=THT]
  J4 = Screw terminal - 2 pins [package=THT]
  X2 = DB15 Connector [package=db15]
  J5 = Screw terminal - 2 pins [package=THT]
  J6 = Screw terminal - 2 pins [package=THT]
  J7 = Screw terminal - 2 pins [package=THT]
  J8 = Screw terminal - 2 pins [package=THT]
  J9 = Screw terminal - 2 pins [package=THT]
  Part2 = BME280 Breakout

nets:
  N1: Part1.A1, R1.Pin_0, X1.5, J5.pin1
  N2: Part1.A4/SDA, X1.14, J8.pin1
  N3: Part1.A5/SCL, X1.15, J8.pin2
  N4: Part1.D9_PWM, X1.11, J7.pin2
  N5: Part1.D10_PWM/SS, U1.IN1
  N6: Part1.D11_PWM/MOSI, U1.IN2
  N7: Part1.D2, Pololu_A1.DIR
  N8: Part1.D3_PWM, Pololu_A1.STEP
  5V: Part1.5V, Pololu_A1.VDD, R1.Pin_1, X1.9, X1.13, U1.VCC, J2.pin1, J6.pin2, J9.pin2
  GND: Part1.GND, Pololu_A1.GND#8, X1.10, X1.12, U1.GND, J2.pin2, J6.pin1, J9.pin1
  N9: S1.L1, X2.7
  N10: S1.COM, X2.6
  N11: S1.L2, X2.5
  N12: Pololu_A1.RESET, Pololu_A1.SLEEP
  N13: Pololu_A1.1B, X1.3, J3.pin1
  N14: Pololu_A1.1A, X1.1, J3.pin2
  N15: Pololu_A1.2A, X1.2, J4.pin1
  N16: Pololu_A1.2B, X1.4, J4.pin2
  N17: Pololu_A1.GND#14, VCC1.-, C1.-
  N18: Pololu_A1.VMOT, VCC1.+, C1.+
  N19: X1.6, J5.pin2
  N20: U1.K2-In, U1.K2-On
  N21: J1.gnd, X2.10
  N22: J1.vcc, X2.9
  N23: J1.pulse, X2.11
  N24: M1.A, X2.4
  N25: M1.C, X2.3
  N26: M1.B, X2.2
  N27: M1.D, X2.1
  N28: X2.12, Part2.GND
  N29: X2.13, Part2.3.3V
  N30: X2.14, Part2.SDI/SDA
  N31: X2.15, Part2.SCK/SCL

custom parts:
  DB15 Connector: DB15 Connector Standard DB15 (D-Sub 15) pc midi or gameport connector. Can be used for old PC compatible joystic.
  2-Channel 5v Relay Shield: 2 Channel 5v Relay Shield w. 2x SPD-06VDC-SD-C
